# Fritzing sketch knock (saved by Fritzing 0.9.3b)
breadboards: 1

parts:
  J1 = Denbit [package=THT]
  R1 = Resistor [tolerance=±5% resistance=1M package=THT]
  J2 = Piezo Speaker

nets:
  N1: J1.pin1, R1.Pin_1, J2.pin2
  N2: J1.pin6, R1.Pin_0, J2.pin1

custom parts:
  Denbit: The Denbit
  Piezo Speaker: Piezo
