# Fritzing sketch servo (saved by Fritzing 0.9.3b)

parts:
  J2 = Denbit [package=THT]
  J3 = Basic Servo

nets:
  N1: J2.pin3, J3.pulse
  N2: J2.pin5, J3.vcc
  N3: J2.pin6, J3.gnd

custom parts:
  Denbit: The Denbit
