# Fritzing sketch servo_knob (saved by Fritzing 0.9.3b)
breadboards: 1

parts:
  R1 = Rotary Potentiometer (Large) [maximum_resistance=10kΩ package=THT]
  J2 = Denbit [package=THT]
  J3 = Basic Servo

nets:
  N1: R1.leg1, J2.pin5, J3.vcc
  N2: R1.wiper, J2.pin1
  N3: R1.leg2, J2.pin6, J3.gnd
  N4: J2.pin3, J3.pulse

custom parts:
  Denbit: The Denbit
