# Fritzing sketch temperature (saved by Fritzing 0.9.3b)
breadboards: 1

parts:
  J2 = Denbit [package=THT]
  R2 = Temperature Sensor (Thermistor) [thermistor_type=NTC package=THT]
  R3 = Resistor [tolerance=±5% resistance=10k package=THT]

nets:
  N1: J2.pin1, R2.pin_0, R3.Pin_0
  N2: J2.pin5, R3.Pin_1
  N3: J2.pin6, R2.pin_1

custom parts:
  Denbit: The Denbit
